# Fritzing sketch Práctica 4 (saved by Fritzing 0.9.10b)
breadboards: 1

parts:
  Driver1 = 28BYJ-48 Driver Module [part_number=ULN2003 package=THT]
  SM1 = 28BYJ-48 Stepper Motor [part_number=28BYJ-48]
  S1 = Pushbutton [package="[THT]"]
  Componente1 = Arduino Uno (Rev3)
  Componente2 = Thumb Joystick

nets:
  N1: Driver1.IN1, Componente1.D8
  N2: Driver1.IN2, Componente1.D9_PWM
  N3: Driver1.IN3, Componente1.D10_PWM/SS
  N4: Driver1.IN4, Componente1.D11_PWM/MOSI
  GND: Driver1.GND, S1.Pin_3, S1.Pin_4, Componente1.GND, Componente2.GND
  5V: Driver1.Vmotor, Componente1.5V, Componente2.VCC
  N5: Driver1.blue-pin, SM1.blue-pin
  N6: Driver1.pink-pin, SM1.pink-pin
  N7: Driver1.yellow-pin, SM1.red-pin
  N8: Driver1.orange-pin, SM1.orange-pin
  N9: Driver1.red-pin, SM1.yellow-pin
  N10: S1.Pin_1, S1.Pin_2, Componente1.D7
  N11: Componente1.D12/MISO, Componente2.SEL

custom parts:
  28BYJ-48 Driver Module: ULN2003 Driver Module for the 28BYJ-48 Unipolar Stepper Motor LED A - Blue wire - Bottom coil left LED B - Pink wire - Top coil left LED C - Yellow wire - Bottom coil right LED D - Orange wire - Top coil right Common rail - red Connector pins: blue - pink - yellow - orange - red Control pins - IN1 to IN4 Power pins - GND & Vmotor (5-12V) On/Off jumper (if removed, power to motor is cut).
  28BYJ-48 Stepper Motor: Unipolar Stepper Motor 28BYJ-48 Top coil - pink & orange Bottom coil - blue & yellow Common rail - red Connector pins: blue - pink - yellow - orange - red

// code stored in the sketch: parte 4.ino
#include <Stepper.h>

const int stepsPerRevolution = 32;
Stepper myStepper(stepsPerRevolution, 8, 10, 9, 11);

const int pul = 7;
const int joy = 12;

int pulState = 0;
int joyState = 0;

void setup() {
  myStepper.setSpeed(500);
  pinMode(pul, INPUT_PULLUP);
  pinMode(joy, INPUT_PULLUP);
  Serial.begin(9600);
}

void loop() {
  pulState = digitalRead(pul);
  joyState = digitalRead(joy);

  if (pulState == LOW) {
    myStepper.step(512);
    delay(500);
  }

  if (joyState == LOW) {
    myStepper.step(-512);
    delay(500);
  }

Serial.print(pulState);
Serial.print("\t");
Serial.println(joyState);
Serial.println("\t");
delay(00);
}
